# Fritzing sketch GEE (saved by Fritzing 0.9.3b)

parts:
  Mod1 = Raspberry Pi Pico W
  LED1 = LED - 5mm [color="Red (633nm)" package="5 mm [THT]"]
  S1 = Round Pushbutton
  J1 = Piezo Speaker
  Componente1 = Thermal Printer
  IC1 = Voltage Regulator [package=78xxl]
  C1 = Capacitor Polarized [package=nippon_f80]
  C2 = Capacitor Polarized [package=nippon_f80]
  JACK1 = 2.1mm Barrel Jack with Terminal Block
  C3 = Capacitor [package=cap-pth-small2]
  R1 = Resistor [tolerance=±5% resistance=220 package="0603 [SMD]"]

nets:
  N1: Mod1.pin_1, Componente1.RXD
  GND: Mod1.pin_3, Mod1.pin_18, Mod1.pin_23, Mod1.pin_28, Mod1.pin_38, Mod1.pin_39, LED1.cathode, S1.leg0, J1.pin2, Componente1.GND#2, IC1.GND, C1.-, C2.-, JACK1.NEG, C3.2
  N2: Mod1.pin_4, R1.Pin_1
  N3: Mod1.pin_9, S1.leg1, C3.1
  N4: Mod1.pin_19, J1.pin1
  N5: Mod1.pin_40, IC1.OUT, C2.+
  N6: LED1.anode, R1.Pin_0
  6V: Componente1.VH, IC1.IN, C1.+, JACK1.POS

custom parts:
  Raspberry Pi Pico W: Raspberry Pi Pico W. Based around the RP2040 microcontroller the Pico W is a low cost microcontroller device bringing Raspberry Pi quality, cost, and easy of use to the microcontroller space. The areas marked KEEPOUT in pcb silkscreen should not have traces running through them to avoid shorts on a soldered in module!
